// Digital circuit 4 Bit Adder.dig as structural Verilog
module _4_Bit_Adder (
  input  B_4,
  input  B_3,
  input  B_2,
  input  B_1,
  input  A_4,
  input  A_3,
  input  A_2,
  input  A_1,
  input  C_i,
  output O_4,
  output O_3,
  output O_2,
  output O_1,
  output C_o
);

  wire add_1_c_o, add_2_c_o, add_3_c_o;

  Add add_1 (.a(B_1), .b(A_1), .c_i(C_i), .s(O_1), .c_o(add_1_c_o));
  Add add_2 (.a(B_2), .b(A_2), .c_i(add_1_c_o), .s(O_2), .c_o(add_2_c_o));
  Add add_3 (.a(B_3), .b(A_3), .c_i(add_2_c_o), .s(O_3), .c_o(add_3_c_o));
  Add add_4 (.a(B_4), .b(A_4), .c_i(add_3_c_o), .s(O_4), .c_o(C_o));
endmodule
