// Digital circuit ALU.dig as structural Verilog
module ALU (
  input  SUB,
  input  B_1,
  input  B_2,
  input  B_3,
  input  B_4,
  input  B_5,
  input  B_6,
  input  B_7,
  input  B_8,
  input  A_1,
  input  A_2,
  input  A_3,
  input  A_4,
  input  A_5,
  input  A_6,
  input  A_7,
  input  A_8,
  input  E,
  output O_7,
  output O_6,
  output O_6_2,
  output O_5,
  output O_4,
  output O_3,
  output O_2,
  output O_1
);

  wire _4_bit_adder_1_o_1, _4_bit_adder_1_o_2, _4_bit_adder_1_o_3, _4_bit_adder_1_o_4, _4_bit_adder_2_c_o,
       _4_bit_adder_2_o_1, _4_bit_adder_2_o_2, _4_bit_adder_2_o_3, _4_bit_adder_2_o_4, not_1_out, xor_1_out,
       xor_2_out, xor_3_out, xor_4_out, xor_5_out, xor_6_out, xor_7_out, xor_8_out;

  xor xor_1 (xor_1_out, B_8, SUB);
  xor xor_2 (xor_2_out, B_7, SUB);
  xor xor_3 (xor_3_out, B_6, SUB);
  xor xor_4 (xor_4_out, B_5, SUB);
  xor xor_5 (xor_5_out, B_4, SUB);
  xor xor_6 (xor_6_out, B_3, SUB);
  xor xor_7 (xor_7_out, B_2, SUB);
  xor xor_8 (xor_8_out, B_1, SUB);
  not not_1 (not_1_out, E);
  _4_Bit_Adder _4_bit_adder_1 (
    .B_4(xor_1_out), .B_3(xor_2_out), .B_2(xor_3_out), .B_1(xor_4_out), .A_4(A_8), .A_3(A_7), .A_2(A_6),
    .A_1(A_5), .C_i(_4_bit_adder_2_c_o), .O_4(_4_bit_adder_1_o_4), .O_3(_4_bit_adder_1_o_3),
    .O_2(_4_bit_adder_1_o_2), .O_1(_4_bit_adder_1_o_1));  // open: C_o
  _4_Bit_Adder _4_bit_adder_2 (
    .B_4(xor_5_out), .B_3(xor_6_out), .B_2(xor_7_out), .B_1(xor_8_out), .A_4(A_4), .A_3(A_3), .A_2(A_2),
    .A_1(A_1), .C_i(SUB), .O_4(_4_bit_adder_2_o_4), .O_3(_4_bit_adder_2_o_3), .O_2(_4_bit_adder_2_o_2),
    .O_1(_4_bit_adder_2_o_1), .C_o(_4_bit_adder_2_c_o));
  assign O_7 = not_1_out ? _4_bit_adder_1_o_4 : 1'bz;  // Driver driver_1
  assign O_6 = not_1_out ? _4_bit_adder_1_o_3 : 1'bz;  // Driver driver_2
  assign O_6_2 = not_1_out ? _4_bit_adder_1_o_2 : 1'bz;  // Driver driver_3
  assign O_5 = not_1_out ? _4_bit_adder_1_o_1 : 1'bz;  // Driver driver_4
  assign O_4 = not_1_out ? _4_bit_adder_2_o_4 : 1'bz;  // Driver driver_5
  assign O_3 = not_1_out ? _4_bit_adder_2_o_3 : 1'bz;  // Driver driver_6
  assign O_2 = not_1_out ? _4_bit_adder_2_o_2 : 1'bz;  // Driver driver_7
  assign O_1 = not_1_out ? _4_bit_adder_2_o_1 : 1'bz;  // Driver driver_8
endmodule
