// Digital circuit Adder.dig as structural Verilog
module Adder (
  input  D1,
  input  D2,
  input  Carry_In,
  output Sum,
  output Carry_Out
);

  wire and_1_out, and_2_out, xor_1_out;

  xor xor_1 (xor_1_out, D1, D2);
  and and_1 (and_1_out, D1, D2);
  xor xor_2 (Sum, xor_1_out, Carry_In);
  and and_2 (and_2_out, xor_1_out, Carry_In);
  or or_1 (Carry_Out, and_2_out, and_1_out);
endmodule
