// Digital circuit 16 Byte RAM.dig as structural Verilog
module _16_Byte_RAM (
  input  A0,
  input  A1,
  input  A2,
  input  A3,
  input  D0,
  input  D1,
  input  D2,
  input  D3,
  input  nCS,
  input  nWE,
  input  D4,
  input  D5,
  input  D6,
  input  D7,
  input  E,
  output Q0,
  output Q1,
  output Q2,
  output Q3,
  output Q4,
  output Q5,
  output Q6,
  output Q7
);

  wire and_1_out, and_2_out, driver_3_out, driver_4_out, driver_5_out, driver_6_out, driver_7_out,
       driver_8_out, driver_9_out, driver_10_out, not_1_out;
  wire [3:0] driver_1_out, driver_2_out, not_2_out, not_3_out, ramdualport_2_d, ramdualport_d;

  not not_1 (not_1_out, E);
  and and_1 (and_1_out, ~nWE, ~nCS);  // And
  and and_2 (and_2_out, nWE, ~nCS);  // And
  RAMDualPort #(.AddrBits(4), .Bits(4)) ramdualport (
    .A({A3, A2, A1, A0}), .Din({D3, D2, D1, D0}), .str(and_1_out), .C(and_1_out), .ld(and_2_out),
    .D(ramdualport_d));
  RAMDualPort #(.AddrBits(4), .Bits(4)) ramdualport_2 (
    .A({A3, A2, A1, A0}), .Din({D7, D6, D5, D4}), .str(and_1_out), .C(and_1_out), .ld(and_2_out),
    .D(ramdualport_2_d));
  assign not_2_out = ~ramdualport_d;  // Not not_2, 4 bits wide
  assign not_3_out = ~ramdualport_2_d;  // Not not_3, 4 bits wide
  assign driver_1_out = and_2_out ? not_2_out : 4'bz;  // Driver driver_1
  assign driver_2_out = and_2_out ? not_3_out : 4'bz;  // Driver driver_2
  assign driver_3_out = not_1_out ? driver_1_out[2] : 1'bz;  // Driver driver_3
  assign driver_4_out = not_1_out ? driver_1_out[3] : 1'bz;  // Driver driver_4
  assign driver_5_out = not_1_out ? driver_2_out[2] : 1'bz;  // Driver driver_5
  assign driver_6_out = not_1_out ? driver_2_out[3] : 1'bz;  // Driver driver_6
  assign driver_7_out = not_1_out ? driver_1_out[0] : 1'bz;  // Driver driver_7
  assign driver_8_out = not_1_out ? driver_1_out[1] : 1'bz;  // Driver driver_8
  assign driver_9_out = not_1_out ? driver_2_out[0] : 1'bz;  // Driver driver_9
  assign driver_10_out = not_1_out ? driver_2_out[1] : 1'bz;  // Driver driver_10
  not not_4 (Q0, driver_7_out);
  not not_5 (Q1, driver_8_out);
  not not_6 (Q2, driver_3_out);
  not not_7 (Q3, driver_4_out);
  not not_8 (Q4, driver_9_out);
  not not_9 (Q5, driver_10_out);
  not not_10 (Q6, driver_5_out);
  not not_11 (Q7, driver_6_out);

  // Notes on the sheet:
  //   A0: pin 1
  //   A1: pin 2
  //   A2: pin 3
  //   A3: pin 4
  //   D0: pin 5
  //   D1: pin 6
  //   D2: pin 7
  //   D3: pin 8
  //   Q0: pin 13
  //   Q1: pin 7
  //   Q2: pin 15
  //   Q3: pin 16
  //   nCS: pin 2, default 1
  //   nWE: pin 3, default 1
  //   D4: pin 9
  //   D5: pin 10
  //   D6: pin 11
  //   D7: pin 12
  //   Q4: pin 17
  //   Q5: pin 18
  //   Q6: pin 19
  //   Q7: pin 20
  //   E: pin 21
endmodule
