// Digital circuit 1 Bit Register.dig as structural Verilog
module _1_Bit_Register (
  input  Load,
  input  D,
  input  Clock,
  output Q
);

  wire and_1_out, and_2_out, d_ff_1_nq, not_1_out, or_1_out;

  not not_1 (not_1_out, Load);
  and and_1 (and_1_out, Q, not_1_out);
  and and_2 (and_2_out, Load, D);
  or or_1 (or_1_out, and_1_out, and_2_out);
  D_FF d_ff_1 (.D(or_1_out), .C(Clock), .Q(Q), .nQ(d_ff_1_nq));
endmodule
