// Digital circuit 8 Bit Register.dig as structural Verilog
module _8_Bit_Register (
  input  Clock,
  input  D5,
  input  D6,
  input  D7,
  input  D8,
  input  Load,
  input  D1,
  input  D2,
  input  D3,
  input  D4,
  input  Enable,
  output out_6,
  output out_7,
  output out_8,
  output out_9,
  output out_15,
  output out_16,
  output out_17,
  output out_18
);

  wire _1_bit_register_1_q, _1_bit_register_2_q, _1_bit_register_3_q, _1_bit_register_4_q,
       _1_bit_register_5_q, _1_bit_register_6_q, _1_bit_register_7_q, _1_bit_register_8_q, not_1_out;

  not not_1 (not_1_out, Enable);
  _1_Bit_Register _1_bit_register_1 (.Load(Load), .D(D1), .Clock(Clock), .Q(_1_bit_register_1_q));
  _1_Bit_Register _1_bit_register_2 (.Load(Load), .D(D2), .Clock(Clock), .Q(_1_bit_register_2_q));
  _1_Bit_Register _1_bit_register_3 (.Load(Load), .D(D3), .Clock(Clock), .Q(_1_bit_register_3_q));
  _1_Bit_Register _1_bit_register_4 (.Load(Load), .D(D4), .Clock(Clock), .Q(_1_bit_register_4_q));
  _1_Bit_Register _1_bit_register_5 (.Load(Load), .D(D5), .Clock(Clock), .Q(_1_bit_register_5_q));
  _1_Bit_Register _1_bit_register_6 (.Load(Load), .D(D6), .Clock(Clock), .Q(_1_bit_register_6_q));
  _1_Bit_Register _1_bit_register_7 (.Load(Load), .D(D7), .Clock(Clock), .Q(_1_bit_register_7_q));
  _1_Bit_Register _1_bit_register_8 (.Load(Load), .D(D8), .Clock(Clock), .Q(_1_bit_register_8_q));
  assign out_15 = not_1_out ? _1_bit_register_1_q : 1'bz;  // Driver driver_1
  assign out_16 = not_1_out ? _1_bit_register_2_q : 1'bz;  // Driver driver_2
  assign out_18 = not_1_out ? _1_bit_register_3_q : 1'bz;  // Driver driver_3
  assign out_17 = not_1_out ? _1_bit_register_4_q : 1'bz;  // Driver driver_4
  assign out_6 = not_1_out ? _1_bit_register_5_q : 1'bz;  // Driver driver_5
  assign out_7 = not_1_out ? _1_bit_register_6_q : 1'bz;  // Driver driver_6
  assign out_9 = not_1_out ? _1_bit_register_7_q : 1'bz;  // Driver driver_7
  assign out_8 = not_1_out ? _1_bit_register_8_q : 1'bz;  // Driver driver_8
endmodule
